// Logisim project cpu.circ as structural Verilog: 2 circuits, main circuit main
module main (
  input  [31:0] RS_READ_VALUE,
  input  [31:0] RT_READ_VALUE,
  input  [31:0] INSTRUCTION,
  input  CLOCK,
  input  RESET,
  output [31:0] t0,
  output [31:0] t1,
  output [31:0] t2,
  output [31:0] t3,
  output [4:0] RS,
  output [4:0] RT,
  output [4:0] Write_Register,
  output [31:0] RD_WRITE_VALUE,
  output RD_WRITE_ENABLE,
  output [23:0] FETCH_ADDRESS
);

  wire ALU_signed_overflow, control_1_alusrc, control_1_branch, control_1_memtoreg, control_1_opalu0,
       control_1_opalu1, control_1_readmem, control_1_regdst, control_1_writemem, control_1_writereg,
       pc_1_or_naw;
  wire [23:0] Incremented, jump_address, multiplexer_1_out;
  wire [31:0] undriven, undriven_2;

  Adder #(.width(24)) adder_1 (.a(FETCH_ADDRESS), .b(24'h1), .out(Incremented));  // open: cin, cout
  Multiplexer #(.width(24)) multiplexer_1 (
    .in0(Incremented), .in1(jump_address), .out(multiplexer_1_out), .sel(pc_1_or_naw));  // open: en
  Register #(.width(24)) register_1 (.D(multiplexer_1_out), .Q(FETCH_ADDRESS), .clk(CLOCK));  // open: en, clr
  alu_main ALU (
    .Switch__S(INSTRUCTION[31:26]), .X(undriven), .Y(undriven_2), .Signed_Overflow(ALU_signed_overflow));  // open: Equal, RESULT
  control control_1 (
    .OPcode(INSTRUCTION[31:26]), .RegDst(control_1_regdst), .ALUSrc(control_1_alusrc),
    .MemToReg(control_1_memtoreg), .WriteReg(control_1_writereg), .ReadMem(control_1_readmem),
    .WriteMem(control_1_writemem), .Branch(control_1_branch), .OpALU1(control_1_opalu1),
    .OpALU0(control_1_opalu0));
  LED led_1 (.in(ALU_signed_overflow));
  mem_main MEM (.CLOCK(CLOCK));  // open: Data_Mem_Addr, Data_Mem_In, ACCESS_BYTE, MEM_WRITE, Data_Mem_Out
  regfile_main RegFile (
    .t0_Value(t0), .t1_Value(t1), .t2_Value(t2), .t3_Value(t3), .clock(CLOCK));  // open: Read_register_1, Read_register_2, write_register, write_data, RegWrite, Read_Data_1, Read_Data_2

  // Other names for the same wires on the sheet: function[5:0] = INSTRUCTION[5:0];
  //   immediate[15:0] = INSTRUCTION[15:0]; word_addressed_target[23:0] = INSTRUCTION[23:0];
  //   shift_amount[4:0] = INSTRUCTION[10:6]; register_d[4:0] = INSTRUCTION[15:11];
  //   register_s[4:0] = INSTRUCTION[25:21]; opcode[5:0] = INSTRUCTION[31:26]

  // Notes on the sheet:
  //   These are outputs/inputs from run.circ
  //   These are outputs to run.circ
endmodule

module control (
  input  [5:0] OPcode,
  output RegDst,
  output ALUSrc,
  output MemToReg,
  output WriteReg,
  output ReadMem,
  output WriteMem,
  output Branch,
  output OpALU1,
  output OpALU0
);

  wire not_1_out, not_2_out, not_3_out, not_4_out, not_5_out, not_6_out, not_7_out, not_8_out, not_9_out,
       not_10_out, not_11_out, not_12_out, not_13_out, not_14_out, not_15_out, not_16_out;

  not not_1 (not_1_out, OPcode[3]);
  not not_2 (not_2_out, OPcode[4]);
  not not_3 (not_3_out, OPcode[2]);
  not not_4 (not_4_out, OPcode[1]);
  not not_5 (not_5_out, OPcode[5]);
  not not_6 (not_6_out, OPcode[0]);
  and and_1 (OpALU1, not_5_out, not_2_out, not_1_out, not_3_out, not_4_out, not_6_out);
  not not_7 (not_7_out, OPcode[4]);
  not not_8 (not_8_out, OPcode[3]);
  not not_9 (not_9_out, OPcode[2]);
  and and_2 (MemToReg, OPcode[5], not_7_out, not_8_out, not_9_out, OPcode[1], OPcode[0]);
  not not_10 (not_10_out, OPcode[2]);
  not not_11 (not_11_out, OPcode[4]);
  and and_3 (WriteMem, OPcode[5], not_11_out, OPcode[3], not_10_out, OPcode[1], OPcode[0]);
  not not_12 (not_12_out, OPcode[4]);
  not not_13 (not_13_out, OPcode[1]);
  not not_14 (not_14_out, OPcode[0]);
  not not_15 (not_15_out, OPcode[3]);
  not not_16 (not_16_out, OPcode[5]);
  and and_4 (Branch, not_16_out, not_12_out, not_15_out, OPcode[2], not_13_out, not_14_out);
  or or_1 (ALUSrc, MemToReg, WriteMem);
  or or_2 (WriteReg, OpALU1, MemToReg);

  assign OpALU0 = Branch;
  assign ReadMem = MemToReg;
  assign RegDst = OpALU1;
endmodule
